# Fritzing sketch DiveInoModules (saved by Fritzing 0.9.3b)
breadboards: 4

parts:
  Part1 = Arduino Mega 2560 (Rev3)
  Q1 = NPN-Transistor [package="TO92 [THT]"]
  LED1 = LED - 5mm [color="Blue (430nm)" package="5 mm [THT]"]
  R1 = Resistor [tolerance=±5% resistance=220 package=THT]
  R2 = Resistor [tolerance=±5% resistance=220 package=THT]
  R3 = Resistor [tolerance=±5% resistance=266k package=THT]
  R4 = Resistor [tolerance=±5% resistance=100k package=THT]
  J1 = female pin header, 2 pins [form="♀ (female)"]
  J3 = female pin header, 4 pins [form="♀ (female)"]
  J6 = male pin header, 3 pins [form="♂ (male)"]
  Part4 = PowerBoost 500 Charger
  J7 = male pin header, 3 pins [form="♂ (male)"]
  SparkFun_LiPo_Fuel_Gauge2 = SparkFun LiPo Fuel Gauge [part_number=TOL-10617]
  S3 = Toggle Switch [package=THT]
  J8 = female pin header, 4 pins [form="♀ (female)"]
  S4 = Reed switch [package=THT]
  R5 = Resistor [tolerance=±5% resistance=10k package=THT]
  J9 = female pin header, 3 pins [form="♀ (female)"]
  J10 = female pin header, 3 pins [form="♀ (female)"]
  RTC1 = female pin header, 4 pins [form="♀ (female)"]
  DS3231_RTC1 = ZS-042 RTC Module
  Pressure_Sensor1 = SparkFun Pressure Sensor Breakout - MS5803-14BA [part_number="SEN-12909 "]
  IPOB1 = female pin header, 4 pins [form="♀ (female)"]
  Data1 = female pin header, 4 pins [form="♀ (female)"]
  Infra1 = Infra red receiver
  Bluefruit1 = Adafruit Bluefruit LE UART Friend [part_number="Adafruit #2479"]
  Pressure1 = female pin header, 4 pins [form="♀ (female)"]
  Piezo1 = Piezo Speaker - PC Mount [part_number=COM-07950]

nets:
  N1: Part1.D21/SCL, J8.pin4, RTC1.pin4, DS3231_RTC1.SCL, Pressure_Sensor1.SCL/SCLK, Data1.pin4, Pressure1.pin4
  N2: Part1.D20/SDA, J8.pin3, RTC1.pin3, DS3231_RTC1.SDA, Pressure_Sensor1.SDA/SDI, Data1.pin3, Pressure1.pin3
  N3: Part1.D19/RX1, Data1.pin2, Bluefruit1.TXO
  N4: Part1.D18/TX1, Data1.pin1, Bluefruit1.RXI
  GND: Part1.GND, Q1.E, LED1.cathode, R3.Pin_0, J3.pin2, J6.pin2, Part4.GND, J7.pin3, SparkFun_LiPo_Fuel_Gauge2.QST, SparkFun_LiPo_Fuel_Gauge2.GND, S3.L2, J8.pin1, S4.pin_2, J9.pin3, J10.pin3, RTC1.pin1, DS3231_RTC1.GND, Pressure_Sensor1.GND, IPOB1.pin2, Infra1.GND, Bluefruit1.GND, Bluefruit1.CTS, Pressure1.pin1, Piezo1.GND
  VCC: Part1.3V3, R2.Pin_0, R4.Pin_0, J3.pin4, RTC1.pin2, DS3231_RTC1.VCC, Pressure_Sensor1.3.3V, IPOB1.pin1, Infra1.VCC, Bluefruit1.VIN, Pressure1.pin2
  N5: Part1.VIN, Part4.5.0V, J8.pin2
  N6: Part1.D2_PWM, IPOB1.pin4, Piezo1.VCC
  N7: Part1.D3_PWM, IPOB1.pin3, Infra1.Data
  N8: Part1.D6_PWM, Q1.C, R2.Pin_1, J3.pin3
  N9: Part1.D7_PWM, R1.Pin_0, J3.pin1
  N10: Q1.B, R3.Pin_1, J1.pin1
  N11: LED1.anode, R1.Pin_1
  N12: R4.Pin_1, J1.pin2
  N13: J6.pin1, Part4.VBAT, SparkFun_LiPo_Fuel_Gauge2.VCC, R5.Pin_0, J9.pin1, J10.pin1
  N14: J6.pin3, SparkFun_LiPo_Fuel_Gauge2.ALT
  N15: Part4.ENABLE, S3.COM, S4.pin_1, R5.Pin_1, J9.pin2, J10.pin2
  N16: J7.pin1, SparkFun_LiPo_Fuel_Gauge2.SDA
  N17: J7.pin2, SparkFun_LiPo_Fuel_Gauge2.SCL

notes:
  Water module
  Switch module
  Power module
  Sensor module

custom parts:
  PowerBoost 500 Charger: The PowerBoost 500C is a little DC/DC boost converter module that can be powered by any 3.7V LiIon/LiPoly battery, and convert the battery output to 5.2V DC for running your 5V projects. At its heart is a TPS61090 boost converter from TI. This boost converter chip has some really nice extras such as low battery detection, 2A internal switch, synchronous conversion, excellent efficiency, and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
  SparkFun LiPo Fuel Gauge: LiPo batteries are a great way to power your projects. They’re small, lightweight, and pack a pretty good punch for their size. Unfortunately, even the best batteries eventually run low on power and when they do it’s often unexpected (and at the worst time). Don’t be caught by surprise next time your board suddenly powers-down! The SparkFun LiPo Fuel Gauge connects your battery to your project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
  SparkFun Pressure Sensor Breakout - MS5803-14BA: This is the MS5803-14BA Pressure Sensor Breakout, a high resolution pressure sensor with both an I2C and SPI interface. This MEMS pressure sensor measures the absolute pressure of the fluid around it which includes air, water, and anything else that acts like a viscous fluid. Depending on how you interpret the data, you can determine altitude, water depth, or any other tasks that require an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
  Adafruit Bluefruit LE UART Friend: The Bluefruit LE UART Friend makes it easy to add Bluetooth Low Energy connectivity to anything with a hardware or software serial port. We even have nice hardware flow control so you won't have to think about losing data. Connect to your Arduino or other microcontroller or even just a standard FTDI cable for debugging and testing.
  Piezo Speaker - PC Mount: This is a small 12mm round speaker that operates around the audible 2kHz range. You can use these speakers to create simple music or user interfaces. Each speaker is PTH solderable and requires an operating voltage of 3.5-5V with a mean current of 35mA max. These speakers also have a typical sound output of 95 dBA and a coil resistance of 42 ±6.3 ohms.
