# Fritzing sketch DiveIno (saved by Fritzing 0.9.3b)
breadboards: 1

parts:
  Main_Board = Arduino Mega 2560 (Rev3)
  On/Off = Toggle Switch [package=THT]
  Bluefruit = Adafruit Bluefruit LE UART Friend [part_number="Adafruit #2479"]
  Base = Resistor [tolerance=±5% resistance=220k package=THT]
  Water = Resistor [tolerance=±5% resistance=22k package=THT]
  Data = female pin header, 4 pins [form="♀ (female)"]
  Water_LED = LED - 5mm [color="Blue (430nm)" package="5 mm [THT]"]
  LED = Resistor [tolerance=±5% resistance=470 package=THT]
  Control = female pin header, 4 pins [form="♀ (female)"]
  Reed = Resistor [tolerance=±5% resistance=10k package=THT]
  Reed_2 = female pin header, 2 pins [form="♀ (female)"]
  Emitter = Resistor [tolerance=±5% resistance=470 package=THT]
  Fuel_Gauge = SparkFun LiPo Fuel Gauge [part_number=TOL-10617]
  Pressure_Sensor = SparkFun Pressure Sensor Breakout - MS5803-14BA [part_number="SEN-12909 "]
  Charger = PowerBoost 500 Charger
  Water_2 = female pin header, 2 pins [form="♀ (female)"]
  DS3231_RTC2 = ZS-042 RTC Module
  Power = female pin header, 3 pins [form="♀ (female)"]
  Transistor = NPN-Transistor [package="TO92 [THT]"]
  Piezo2 = Piezo Speaker - PC Mount [part_number=COM-07950]
  Infra2 = Infra red receiver

nets:
  N1: Main_Board.D21/SCL, Main_Board.SCL, Data.pin4, Fuel_Gauge.SCL, Pressure_Sensor.SCL/SCLK, DS3231_RTC2.SCL
  N2: Main_Board.D20/SDA, Main_Board.SDA, Data.pin3, Fuel_Gauge.SDA, Pressure_Sensor.SDA/SDI, DS3231_RTC2.SDA
  N3: Main_Board.D19/RX1, Bluefruit.TXO, Data.pin2
  N4: Main_Board.D18/TX1, Bluefruit.RXI, Data.pin1
  VCC: Main_Board.3V3, Bluefruit.VIN, Water.Pin_0, Emitter.Pin_0, Pressure_Sensor.3.3V, DS3231_RTC2.VCC, Power.pin1, Infra2.VCC
  GND: Main_Board.GND, On/Off.L2, Bluefruit.GND, Bluefruit.CTS, Base.Pin_0, Water_LED.cathode, Reed_2.pin2, Fuel_Gauge.QST, Fuel_Gauge.GND, Pressure_Sensor.GND, Charger.GND, DS3231_RTC2.GND, Power.pin2, Transistor.E, Piezo2.GND, Infra2.GND
  N5: Main_Board.VIN, Charger.5.0V, Power.pin3
  N6: Main_Board.D2_PWM, Control.pin4, Piezo2.VCC
  N7: Main_Board.D3_PWM, Control.pin3, Infra2.Data
  N8: Main_Board.D4_PWM, Control.pin2, Emitter.Pin_1, Transistor.C
  N9: Main_Board.D5_PWM, LED.Pin_0, Control.pin1
  N10: On/Off.COM, Reed.Pin_0, Reed_2.pin1, Charger.ENABLE
  N11: Base.Pin_1, Water_2.pin1, Transistor.B
  N12: Water.Pin_1, Water_2.pin2
  N13: Water_LED.anode, LED.Pin_1
  N14: Reed.Pin_1, Fuel_Gauge.VCC, Charger.VBAT

notes:
  DiveIno

custom parts:
  Adafruit Bluefruit LE UART Friend: The Bluefruit LE UART Friend makes it easy to add Bluetooth Low Energy connectivity to anything with a hardware or software serial port. We even have nice hardware flow control so you won't have to think about losing data. Connect to your Arduino or other microcontroller or even just a standard FTDI cable for debugging and testing.
  SparkFun LiPo Fuel Gauge: LiPo batteries are a great way to power your projects. They’re small, lightweight, and pack a pretty good punch for their size. Unfortunately, even the best batteries eventually run low on power and when they do it’s often unexpected (and at the worst time). Don’t be caught by surprise next time your board suddenly powers-down! The SparkFun LiPo Fuel Gauge connects your battery to your project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
  SparkFun Pressure Sensor Breakout - MS5803-14BA: This is the MS5803-14BA Pressure Sensor Breakout, a high resolution pressure sensor with both an I2C and SPI interface. This MEMS pressure sensor measures the absolute pressure of the fluid around it which includes air, water, and anything else that acts like a viscous fluid. Depending on how you interpret the data, you can determine altitude, water depth, or any other tasks that require an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
  PowerBoost 500 Charger: The PowerBoost 500C is a little DC/DC boost converter module that can be powered by any 3.7V LiIon/LiPoly battery, and convert the battery output to 5.2V DC for running your 5V projects. At its heart is a TPS61090 boost converter from TI. This boost converter chip has some really nice extras such as low battery detection, 2A internal switch, synchronous conversion, excellent efficiency, and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
  Piezo Speaker - PC Mount: This is a small 12mm round speaker that operates around the audible 2kHz range. You can use these speakers to create simple music or user interfaces. Each speaker is PTH solderable and requires an operating voltage of 3.5-5V with a mean current of 35mA max. These speakers also have a typical sound output of 95 dBA and a coil resistance of 42 ±6.3 ohms.
