# Fritzing sketch SwitchModule (saved by Fritzing 0.9.3b)
circuit board: 1.5cm x 2cm
breadboards: 1

parts:
  Power = female pin header, 3 pins [form="♀ (female)"]
  Reed = Reed switch [package=THT]
  10k = Resistor [tolerance=±5% resistance=10k package=THT]

nets:
  N1: Power.pin1, 10k.Pin_0
  N2: Power.pin2, Reed.pin_1, 10k.Pin_1
  N3: Power.pin3, Reed.pin_2
