# Fritzing sketch PowerModule (saved by Fritzing 0.9.3b)
breadboards: 1

parts:
  SparkFun_LiPo_Fuel_Gauge1 = SparkFun LiPo Fuel Gauge [part_number=TOL-10617]
  Part1 = PowerBoost 500 Charger
  J1 = male pin header, 3 pins [form="♂ (male)"]
  J2 = male pin header, 3 pins [form="♂ (male)"]
  S1 = Toggle Switch [package=THT]
  Part2 = Arduino Mega 2560 (Rev3)
  J3 = female pin header, 4 pins [form="♀ (female)"]
  J4 = female pin header, 3 pins [form="♀ (female)"]

nets:
  N1: SparkFun_LiPo_Fuel_Gauge1.SDA, J1.pin1
  N2: SparkFun_LiPo_Fuel_Gauge1.SCL, J1.pin2
  N3: SparkFun_LiPo_Fuel_Gauge1.QST, J1.pin3
  N4: SparkFun_LiPo_Fuel_Gauge1.VCC, Part1.VBAT, J2.pin1, S1.L1, J4.pin1
  GND: SparkFun_LiPo_Fuel_Gauge1.GND, Part1.GND, J2.pin2, S1.L2, Part2.GND, J3.pin1, J4.pin3
  N5: SparkFun_LiPo_Fuel_Gauge1.ALT, J2.pin3
  N6: Part1.ENABLE, S1.COM, J4.pin2
  N7: Part1.5.0V, Part2.VIN, J3.pin2
  N8: Part2.D21/SCL, J3.pin4
  N9: Part2.D20/SDA, J3.pin3

custom parts:
  SparkFun LiPo Fuel Gauge: LiPo batteries are a great way to power your projects. They’re small, lightweight, and pack a pretty good punch for their size. Unfortunately, even the best batteries eventually run low on power and when they do it’s often unexpected (and at the worst time). Don’t be caught by surprise next time your board suddenly powers-down! The SparkFun LiPo Fuel Gauge connects your battery to your project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
  PowerBoost 500 Charger: The PowerBoost 500C is a little DC/DC boost converter module that can be powered by any 3.7V LiIon/LiPoly battery, and convert the battery output to 5.2V DC for running your 5V projects. At its heart is a TPS61090 boost converter from TI. This boost converter chip has some really nice extras such as low battery detection, 2A internal switch, synchronous conversion, excellent efficiency, and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
