# Fritzing sketch SensorModule (saved by Fritzing 0.9.3b)
circuit board: 4.50342cm x 3cm
breadboards: 1

parts:
  Arduino_Mega_2560 = Arduino Mega 2560 (Rev3)
  Pressure_Sensor = SparkFun Pressure Sensor Breakout - MS5803-14BA [part_number="SEN-12909 "]
  IPOB = female pin header, 4 pins [form="♀ (female)"]
  Data = female pin header, 4 pins [form="♀ (female)"]
  Infra = Infra red receiver
  DS3231_RTC = ZS-042 RTC Module
  Piezo = Piezo Speaker - PC Mount [part_number=COM-07950]
  Pressure = female pin header, 4 pins [form="♀ (female)"]
  RTC = female pin header, 4 pins [form="♀ (female)"]
  Bluefruit = Adafruit Bluefruit LE UART Friend [part_number="Adafruit #2479"]

nets:
  N1: Arduino_Mega_2560.D21/SCL, Pressure_Sensor.SCL/SCLK, Data.pin4, DS3231_RTC.SCL, Pressure.pin4, RTC.pin4
  N2: Arduino_Mega_2560.D20/SDA, Pressure_Sensor.SDA/SDI, Data.pin3, DS3231_RTC.SDA, Pressure.pin3, RTC.pin3
  N3: Arduino_Mega_2560.D19/RX1, Data.pin2, Bluefruit.TXO
  N4: Arduino_Mega_2560.D18/TX1, Data.pin1, Bluefruit.RXI
  VCC: Arduino_Mega_2560.3V3, Pressure_Sensor.3.3V, IPOB.pin1, Infra.VCC, DS3231_RTC.VCC, Pressure.pin2, RTC.pin2, Bluefruit.VIN
  GND: Arduino_Mega_2560.GND, Pressure_Sensor.GND, IPOB.pin2, Infra.GND, DS3231_RTC.GND, Piezo.GND, Pressure.pin1, RTC.pin1, Bluefruit.GND, Bluefruit.CTS
  N5: Arduino_Mega_2560.D2_PWM, IPOB.pin4, Piezo.VCC
  N6: Arduino_Mega_2560.D3_PWM, IPOB.pin3, Infra.Data

custom parts:
  SparkFun Pressure Sensor Breakout - MS5803-14BA: This is the MS5803-14BA Pressure Sensor Breakout, a high resolution pressure sensor with both an I2C and SPI interface. This MEMS pressure sensor measures the absolute pressure of the fluid around it which includes air, water, and anything else that acts like a viscous fluid. Depending on how you interpret the data, you can determine altitude, water depth, or any other tasks that require an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
  Piezo Speaker - PC Mount: This is a small 12mm round speaker that operates around the audible 2kHz range. You can use these speakers to create simple music or user interfaces. Each speaker is PTH solderable and requires an operating voltage of 3.5-5V with a mean current of 35mA max. These speakers also have a typical sound output of 95 dBA and a coil resistance of 42 ±6.3 ohms.
  Adafruit Bluefruit LE UART Friend: The Bluefruit LE UART Friend makes it easy to add Bluetooth Low Energy connectivity to anything with a hardware or software serial port. We even have nice hardware flow control so you won't have to think about losing data. Connect to your Arduino or other microcontroller or even just a standard FTDI cable for debugging and testing.
