# Fritzing sketch SwitchModule (saved by Fritzing 0.9.3b)
breadboards: 1

parts:
  S3 = Reed switch [package=THT]
  R2 = Resistor [tolerance=±5% resistance=10k package=THT]
  J6 = female pin header, 3 pins [form="♀ (female)"]

nets:
  N1: S3.pin_1, R2.Pin_1, J6.pin2
  N2: S3.pin_2, J6.pin3
  N3: R2.Pin_0, J6.pin1
