# Fritzing sketch WaterModule (saved by Fritzing 0.9.3b)
circuit board: 3cm x 3cm
breadboards: 1

parts:
  Part2 = Arduino Mega 2560 (Rev3)
  NPN = NPN-Transistor [package="TO92 [THT]"]
  LED = LED - 5mm [color="Blue (430nm)" package="5 mm [THT]"]
  220 = Resistor [tolerance=±5% resistance=220 package=THT]
  220_2 = Resistor [tolerance=±5% resistance=220 package=THT]
  250k = Resistor [tolerance=±5% resistance=250k package=THT]
  100k = Resistor [tolerance=±5% resistance=100k package=THT]
  Water = female pin header, 2 pins [form="♀ (female)"]
  Board = female pin header, 4 pins [form="♀ (female)"]

nets:
  N1: Part2.GND, NPN.E, LED.cathode, 250k.Pin_0, Board.pin2
  N2: Part2.3V3, 220_2.Pin_0, 100k.Pin_0, Board.pin4
  N3: Part2.D6_PWM, NPN.C, 220_2.Pin_1, Board.pin3
  N4: Part2.D7_PWM, 220.Pin_0, Board.pin1
  N5: NPN.B, 250k.Pin_1, Water.pin1
  N6: LED.anode, 220.Pin_1
  N7: 100k.Pin_1, Water.pin2

notes:
  Water module
